# Fritzing sketch rangkaian iot (saved by Fritzing 0.9.5d)
breadboards: 1

parts:
  WeMos_D1_Mini1 = WeMos D1 Mini
  Part1 = Soil Moisture Sensor
  HC-SR04_Sensor_1 = HC-SR04 Ultrasonic Distance Sensor
  WATER_PUMP1 = water pump/motor  # not connected
  WATER_PUMP2 = water pump/motor  # not connected
  A1 = 2 channel relay module [package=THT]

nets:
  N1: WeMos_D1_Mini1.D7, A1.pin_15
  N2: WeMos_D1_Mini1.D8, A1.pin_16
  VCC: Part1.VCC, HC-SR04_Sensor_1.VCC, A1.pin_4, A1.pin_13
  GND: Part1.GND, HC-SR04_Sensor_1.GND, A1.pin_14

custom parts:
  water pump/motor: WATER PUMP BY ARDUBLOCKTR
  2 channel relay module: 2 channel Relay Module 5V 12V 24V High and Low Level Trigger Relay Control With Optocoupler Two Way relays DC 5 V 12 V 24 V Volt.
